// Logisim project Полусумматор.circ as structural Verilog: 6 circuits, main circuit Полусумматор
module \Полусумматор  (
  input  \А ,
  input  \В ,
  output \Сумма ,
  output \Перенос 
);

  xor xor_1 (\Сумма , \А , \В );
  and and_1 (\Перенос , \А , \В );
endmodule

module \Сумматор  (
  input  A,
  input  B,
  input  C,
  output \Сумма ,
  output \Перенос 
);

  wire \полусумматор_1_перенос , \полусумматор_1_сумма , \полусумматор_2_перенос ;

  \Полусумматор  \u_полусумматор_1  (
    .\Сумма (\полусумматор_1_сумма ), .\Перенос (\полусумматор_1_перенос ), .\А (A), .\В (B));
  \Полусумматор  \u_полусумматор_2  (
    .\Сумма (\Сумма ), .\Перенос (\полусумматор_2_перенос ), .\А (C), .\В (\полусумматор_1_сумма ));
  or or_1 (\Перенос , \полусумматор_2_перенос , \полусумматор_1_перенос );
endmodule

module \Сумматор_с_вычитанием  (
  input  [7:0] A,
  input  [7:0] B,
  input  in_3,
  output [8:0] out_4
);

  wire \инвертор_1_out_3 , \инвертор_1_out_4 , \инвертор_1_out_5 , \инвертор_1_out_6 , \инвертор_1_out_7 ,
       \инвертор_1_out_8 , \инвертор_1_out_9 , \инвертор_1_out_10 , \сумматор_1_перенос ,
       \сумматор_2_перенос , \сумматор_3_перенос , \сумматор_4_перенос , \сумматор_5_перенос ,
       \сумматор_6_перенос , \сумматор_7_перенос , \сумматор_8_перенос ;

  // Probe on A
  \Инвертор  \u_инвертор_1  (
    .in_2(in_3), .in_1(B), .out_3(\инвертор_1_out_3 ), .out_4(\инвертор_1_out_4 ),
    .out_5(\инвертор_1_out_5 ), .out_6(\инвертор_1_out_6 ), .out_7(\инвертор_1_out_7 ),
    .out_8(\инвертор_1_out_8 ), .out_9(\инвертор_1_out_9 ), .out_10(\инвертор_1_out_10 ));
  xor xor_1 (out_4[8], in_3, \сумматор_4_перенос );
  \Сумматор  \u_сумматор_1  (
    .\Сумма (out_4[4]), .\Перенос (\сумматор_1_перенос ), .A(A[4]), .B(\инвертор_1_out_6 ),
    .C(\сумматор_8_перенос ));
  \Сумматор  \u_сумматор_2  (
    .\Сумма (out_4[5]), .\Перенос (\сумматор_2_перенос ), .A(A[5]), .B(\инвертор_1_out_5 ),
    .C(\сумматор_1_перенос ));
  \Сумматор  \u_сумматор_3  (
    .\Сумма (out_4[6]), .\Перенос (\сумматор_3_перенос ), .A(A[6]), .B(\инвертор_1_out_4 ),
    .C(\сумматор_2_перенос ));
  \Сумматор  \u_сумматор_4  (
    .\Сумма (out_4[7]), .\Перенос (\сумматор_4_перенос ), .A(A[7]), .B(\инвертор_1_out_3 ),
    .C(\сумматор_3_перенос ));
  \Сумматор  \u_сумматор_5  (
    .\Сумма (out_4[0]), .\Перенос (\сумматор_5_перенос ), .A(A[0]), .B(\инвертор_1_out_10 ), .C(in_3));
  \Сумматор  \u_сумматор_6  (
    .\Сумма (out_4[1]), .\Перенос (\сумматор_6_перенос ), .A(A[1]), .B(\инвертор_1_out_9 ),
    .C(\сумматор_5_перенос ));
  \Сумматор  \u_сумматор_7  (
    .\Сумма (out_4[2]), .\Перенос (\сумматор_7_перенос ), .A(A[2]), .B(\инвертор_1_out_8 ),
    .C(\сумматор_6_перенос ));
  \Сумматор  \u_сумматор_8  (
    .\Сумма (out_4[3]), .\Перенос (\сумматор_8_перенос ), .A(A[3]), .B(\инвертор_1_out_7 ),
    .C(\сумматор_7_перенос ));
  // Probe on out_4
endmodule

module \Сумматор_8_бит  (
  input  [7:0] A,
  input  [7:0] B,
  input  in_3,
  output out_4,
  output [7:0] out_5
);

  wire \сумматор_1_перенос , \сумматор_2_перенос , \сумматор_3_перенос , \сумматор_5_перенос ,
       \сумматор_6_перенос , \сумматор_7_перенос , \сумматор_8_перенос ;

  // Probe on A
  // Probe on B
  \Сумматор  \u_сумматор_1  (
    .\Сумма (out_5[4]), .\Перенос (\сумматор_1_перенос ), .A(A[4]), .B(B[4]), .C(\сумматор_8_перенос ));
  \Сумматор  \u_сумматор_2  (
    .\Сумма (out_5[5]), .\Перенос (\сумматор_2_перенос ), .A(A[5]), .B(B[5]), .C(\сумматор_1_перенос ));
  \Сумматор  \u_сумматор_3  (
    .\Сумма (out_5[6]), .\Перенос (\сумматор_3_перенос ), .A(A[6]), .B(B[6]), .C(\сумматор_2_перенос ));
  \Сумматор  \u_сумматор_4  (.\Сумма (out_5[7]), .\Перенос (out_4), .A(A[7]), .B(B[7]), .C(\сумматор_3_перенос ));
  \Сумматор  \u_сумматор_5  (.\Сумма (out_5[0]), .\Перенос (\сумматор_5_перенос ), .A(A[0]), .B(B[0]), .C(in_3));
  \Сумматор  \u_сумматор_6  (
    .\Сумма (out_5[1]), .\Перенос (\сумматор_6_перенос ), .A(A[1]), .B(B[1]), .C(\сумматор_5_перенос ));
  \Сумматор  \u_сумматор_7  (
    .\Сумма (out_5[2]), .\Перенос (\сумматор_7_перенос ), .A(A[2]), .B(B[2]), .C(\сумматор_6_перенос ));
  \Сумматор  \u_сумматор_8  (
    .\Сумма (out_5[3]), .\Перенос (\сумматор_8_перенос ), .A(A[3]), .B(B[3]), .C(\сумматор_7_перенос ));
  // Probe on out_5
endmodule

module \Инвертор  (
  input  [7:0] in_1,
  input  in_2,
  output out_3,
  output out_4,
  output out_5,
  output out_6,
  output out_7,
  output out_8,
  output out_9,
  output out_10
);

  xor xor_1 (out_3, in_2, in_1[7]);
  xor xor_2 (out_4, in_2, in_1[6]);
  xor xor_3 (out_5, in_2, in_1[5]);
  xor xor_4 (out_6, in_2, in_1[4]);
  xor xor_5 (out_7, in_2, in_1[3]);
  xor xor_6 (out_8, in_2, in_1[2]);
  xor xor_7 (out_9, in_2, in_1[1]);
  xor xor_8 (out_10, in_2, in_1[0]);
endmodule

module \Умножитель  (
  input  [3:0] in_1,
  input  [3:0] in_2,
  output out_3,
  output out_4,
  output out_5,
  output out_6,
  output out_7,
  output out_8,
  output out_9,
  output out_10
);

  wire and_1_out, and_2_out, and_3_out, and_4_out, and_5_out, and_6_out, and_7_out, and_8_out, and_9_out,
       and_10_out, and_11_out, and_12_out, and_13_out, and_14_out, and_15_out, \сумматор_2_перенос ,
       \сумматор_2_сумма , \сумматор_3_перенос , \сумматор_4_перенос , \сумматор_4_сумма ,
       \сумматор_5_перенос , \сумматор_5_сумма , \сумматор_6_перенос , \сумматор_7_перенос ,
       \сумматор_7_сумма , \сумматор_8_перенос , \сумматор_8_сумма , \сумматор_9_перенос ,
       \сумматор_10_перенос , \сумматор_10_сумма , \сумматор_11_перенос , \сумматор_12_перенос ;

  // Probe on in_1
  // Probe on {{2{out_4}}, out_5, out_6, out_7, out_8, out_9, out_10}
  and and_1 (and_1_out, in_1[3], in_2[3]);
  and and_2 (and_2_out, in_1[3], in_2[2]);
  \Сумматор  \u_сумматор_1  (
    .\Сумма (out_4), .\Перенос (out_3), .A(\сумматор_2_перенос ), .B(and_1_out), .C(\сумматор_3_перенос ));
  and and_3 (and_3_out, in_1[3], in_2[1]);
  \Сумматор  \u_сумматор_2  (
    .\Сумма (\сумматор_2_сумма ), .\Перенос (\сумматор_2_перенос ), .A(\сумматор_4_перенос ), .B(and_2_out),
    .C(\сумматор_5_перенос ));
  and and_4 (and_4_out, in_1[2], in_2[3]);
  and and_5 (and_5_out, in_1[2], in_2[2]);
  \Сумматор  \u_сумматор_3  (
    .\Сумма (out_5), .\Перенос (\сумматор_3_перенос ), .A(and_4_out), .B(\сумматор_2_сумма ),
    .C(\сумматор_6_перенос ));
  and and_6 (and_6_out, in_1[2], in_2[1]);
  \Сумматор  \u_сумматор_4  (
    .\Сумма (\сумматор_4_сумма ), .\Перенос (\сумматор_4_перенос ), .A(and_3_out), .B(1'b0),
    .C(\сумматор_7_перенос ));
  \Сумматор  \u_сумматор_5  (
    .\Сумма (\сумматор_5_сумма ), .\Перенос (\сумматор_5_перенос ), .A(\сумматор_4_сумма ), .B(and_5_out),
    .C(\сумматор_8_перенос ));
  and and_7 (and_7_out, in_1[1], in_2[3]);
  \Сумматор  \u_сумматор_6  (
    .\Сумма (out_6), .\Перенос (\сумматор_6_перенос ), .A(and_7_out), .B(\сумматор_5_сумма ),
    .C(\сумматор_9_перенос ));
  and and_8 (and_8_out, in_1[3], in_2[0]);
  \Сумматор  \u_сумматор_7  (
    .\Сумма (\сумматор_7_сумма ), .\Перенос (\сумматор_7_перенос ), .A(and_8_out), .B(and_6_out),
    .C(\сумматор_10_перенос ));
  and and_9 (and_9_out, in_1[1], in_2[2]);
  \Сумматор  \u_сумматор_8  (
    .\Сумма (\сумматор_8_сумма ), .\Перенос (\сумматор_8_перенос ), .A(\сумматор_7_сумма ), .B(and_9_out),
    .C(\сумматор_11_перенос ));
  and and_10 (and_10_out, in_1[1], in_2[1]);
  and and_11 (and_11_out, in_1[0], in_2[3]);
  and and_12 (and_12_out, in_1[2], in_2[0]);
  and and_13 (and_13_out, in_1[0], in_2[2]);
  \Сумматор  \u_сумматор_9  (
    .\Сумма (out_7), .\Перенос (\сумматор_9_перенос ), .A(and_11_out), .B(\сумматор_8_сумма ), .C(1'b0));
  and and_14 (and_14_out, in_1[0], in_2[1]);
  \Сумматор  \u_сумматор_10  (
    .\Сумма (\сумматор_10_сумма ), .\Перенос (\сумматор_10_перенос ), .A(and_12_out), .B(and_10_out),
    .C(\сумматор_12_перенос ));
  \Сумматор  \u_сумматор_11  (
    .\Сумма (out_8), .\Перенос (\сумматор_11_перенос ), .A(\сумматор_10_сумма ), .B(and_13_out), .C(1'b0));
  and and_15 (and_15_out, in_1[1], in_2[0]);
  \Сумматор  \u_сумматор_12  (
    .\Сумма (out_9), .\Перенос (\сумматор_12_перенос ), .A(and_15_out), .B(and_14_out), .C(1'b0));
  and and_16 (out_10, in_1[0], in_2[0]);
  // Probe on in_2
endmodule
